// Logisim project Mic-2 Architeture.circ as structural Verilog: 19 circuits, main circuit Mic-2 (8bits Architecture)
module Mic_2__8bits_Architecture (
  input  switch_auto_manual,
  input  manual_push_button,
  input  [7:0] Binary_Switches,
  input  [7:0] programmable_data_inputs_switches,
  input  [7:0] programmable_address_switches,
  input  run_programming_mode_switch
);

  wire CLK, cpu_1_ind, cpu_1_outi, cpu_1_r_i, cpu_1_rdi, cpu_1_rdo, Enter_Button_out, HLT1, HLT2,
       keyboard_input_1_read_state_indicator, not_1_out, not_2_out, or_1_out, RAM_progamming_push_button_out,
       system_clock_out;
  wire [7:0] cpu_1_memory_address_bus, cpu_1_memory_data__bus_out, cpu_1_output_port,
       display_1_hundreds_digit, display_1_ones_digit, display_1_signe_digit, display_1_tens_digit,
       keyboard_input_1_keyboard_value, main_memory_1_memory_data_bus_2;

  Clock_part system_clock (.out(system_clock_out));
  CPU cpu_1 (
    .Memory_Address_Bus(cpu_1_memory_address_bus), .Input_Port(keyboard_input_1_keyboard_value),
    .Memory_Data__Bus_Out(cpu_1_memory_data__bus_out), .RDO(cpu_1_rdo), .RDI(cpu_1_rdi), .R_I(cpu_1_r_i),
    .OUTI(cpu_1_outi), .IND(cpu_1_ind), .Clk(CLK), .Halt(HLT1),
    .Memory_Data__Bus_In(main_memory_1_memory_data_bus_2), .Output_Port(cpu_1_output_port));
  LED led_1 (.in(switch_auto_manual));
  or or_1 (or_1_out, HLT1, HLT2);
  LED led_2 (.in(not_1_out));
  not not_1 (not_1_out, switch_auto_manual);
  Clock clock_1 (
    .clk(system_clock_out), .switch(switch_auto_manual), .manual(manual_push_button), .hlt(or_1_out),
    .clock_output(CLK));
  LED led_3 (.in(CLK));
  LED run_mode_on (.in(not_2_out));
  LED programming_mode_on (.in(run_programming_mode_switch));
  Main_Memory main_memory_1 (
    .Memory_Address_Bus(cpu_1_memory_address_bus), .Memory_Data_Bus(cpu_1_memory_data__bus_out), .Clk(CLK),
    .R_I(cpu_1_r_i), .RDI(cpu_1_rdi), .RDO(cpu_1_rdo),
    .progrmmable_data_inputs_switches(programmable_data_inputs_switches),
    .programmable_address_switches(programmable_address_switches),
    .run_programming_mode_switch(run_programming_mode_switch),
    .RAM_progamming_push_button(RAM_progamming_push_button_out),
    .Memory_Data_Bus_2(main_memory_1_memory_data_bus_2));
  Button RAM_progamming_push_button (.out(RAM_progamming_push_button_out));
  not not_2 (not_2_out, run_programming_mode_switch);
  Display display_1 (
    .Output_Display_Value(cpu_1_output_port), .Ones_Digit(display_1_ones_digit),
    .Tens_Digit(display_1_tens_digit), .Hundreds_Digit(display_1_hundreds_digit),
    .Signe_Digit(display_1_signe_digit), .CLK(CLK), .OUTI(cpu_1_outi));
  Keyboard_Input keyboard_input_1 (
    .Keyboard_Value(keyboard_input_1_keyboard_value), .Binary_Keyboard(Binary_Switches),
    .Enter_Push_Button(Enter_Button_out), .IND(cpu_1_ind), .HLT(HLT2),
    .Read_State_Indicator(keyboard_input_1_read_state_indicator));
  _7_Segment_Display u_7_segment_display_1 (
    .g(display_1_signe_digit[6]), .f(display_1_signe_digit[5]), .a(display_1_signe_digit[0]),
    .b(display_1_signe_digit[1]), .e(display_1_signe_digit[4]), .d(display_1_signe_digit[3]),
    .c(display_1_signe_digit[2]));  // open: dp
  Button Enter_Button (.out(Enter_Button_out));
  LED Keyboard_Full (.in(keyboard_input_1_read_state_indicator));
  _7_Segment_Display u_7_segment_display_2 (
    .g(display_1_hundreds_digit[6]), .f(display_1_hundreds_digit[5]), .a(display_1_hundreds_digit[0]),
    .b(display_1_hundreds_digit[1]), .e(display_1_hundreds_digit[4]), .d(display_1_hundreds_digit[3]),
    .c(display_1_hundreds_digit[2]));  // open: dp
  _7_Segment_Display u_7_segment_display_3 (
    .g(display_1_tens_digit[6]), .f(display_1_tens_digit[5]), .a(display_1_tens_digit[0]),
    .b(display_1_tens_digit[1]), .e(display_1_tens_digit[4]), .d(display_1_tens_digit[3]),
    .c(display_1_tens_digit[2]));  // open: dp
  _7_Segment_Display u_7_segment_display_4 (
    .g(display_1_ones_digit[6]), .f(display_1_ones_digit[5]), .a(display_1_ones_digit[0]),
    .b(display_1_ones_digit[1]), .e(display_1_ones_digit[4]), .d(display_1_ones_digit[3]),
    .c(display_1_ones_digit[2]));  // open: dp

  // Notes on the sheet:
  //   automatic
  //   manual
  //   halt signal
  //   Memory Data In Bus 
  //   RDO (RAM Data Out - RAM Read Signal) 
  //   RDI (RAM Data In - RAM Write Signal) 
  //   R@I (RAM Address In - RAM Write Address Signal) 
  //   Memory Data Out Bus  
  //   Memory Address Bus
  //   clock signal
  //   OUTI (Out input - Write Output Value Signal)
  //   Display Output Value Bus
  //   IND (Input Data Signal - Read Input Value Signal) 
  //   Binary keyboard Inpt Bus 
endmodule

// FullAdder
module Full_Adder (
  input  Cin,
  input  A,
  input  B,
  output S,
  output Cout
);

  wire and_1_out, and_2_out, and_3_out;

  xor xor_1 (S, A, B, Cin);
  and and_1 (and_1_out, A, B);
  and and_2 (and_2_out, A, Cin);
  and and_3 (and_3_out, B, Cin);
  or or_1 (Cout, and_1_out, and_2_out, and_3_out);
endmodule

// Adder
module Adder_8bits (
  input  Cin,
  input  [7:0] A,
  input  [7:0] B,
  output [7:0] out_4,
  output Cout
);

  wire full_adder_1_cout, full_adder_2_cout, full_adder_3_cout, full_adder_4_cout, full_adder_5_cout,
       full_adder_6_cout, full_adder_7_cout;

  Full_Adder full_adder_1 (.A(A[0]), .B(B[0]), .S(out_4[0]), .Cin(Cin), .Cout(full_adder_1_cout));
  Full_Adder full_adder_2 (.A(A[1]), .B(B[1]), .S(out_4[1]), .Cin(full_adder_1_cout), .Cout(full_adder_2_cout));
  Full_Adder full_adder_3 (.A(A[2]), .B(B[2]), .S(out_4[2]), .Cin(full_adder_2_cout), .Cout(full_adder_3_cout));
  Full_Adder full_adder_4 (.A(A[3]), .B(B[3]), .S(out_4[3]), .Cin(full_adder_3_cout), .Cout(full_adder_4_cout));
  Full_Adder full_adder_5 (.A(A[4]), .B(B[4]), .S(out_4[4]), .Cin(full_adder_4_cout), .Cout(full_adder_5_cout));
  Full_Adder full_adder_6 (.A(A[5]), .B(B[5]), .S(out_4[5]), .Cin(full_adder_5_cout), .Cout(full_adder_6_cout));
  Full_Adder full_adder_7 (.A(A[6]), .B(B[6]), .S(out_4[6]), .Cin(full_adder_6_cout), .Cout(full_adder_7_cout));
  Full_Adder full_adder_8 (.A(A[7]), .B(B[7]), .S(out_4[7]), .Cin(full_adder_7_cout), .Cout(Cout));
endmodule

module ALU (
  input  F2,
  input  F1,
  input  F0,
  input  [7:0] A,
  input  [7:0] B,
  output [7:0] OUT,
  output Zero,
  output Cout
);

  wire and_3_out, or_2_out;
  wire [7:0] adder_8bits_1_out_4, and_1_out, and_2_out, not_1_out, or_1_out, xor_1_out;
  wire [7:7] and_4_out, not_2_out;

  assign and_1_out = {8{not_2_out[7]}} & A;  // AND_Gate and_1, 8 bits wide
  assign xor_1_out = B ^ {8{and_4_out[7]}};  // XOR_Gate xor_1, 8 bits wide
  assign and_2_out = A & B;  // AND_Gate and_2, 8 bits wide
  assign or_1_out = A | B;  // OR_Gate or_1, 8 bits wide
  assign not_1_out = ~A;  // NOT_Gate not_1, 8 bits wide
  Adder_8bits adder_8bits_1 (.A(and_1_out), .B(xor_1_out), .out_4(adder_8bits_1_out_4), .Cin(or_2_out), .Cout(Cout));
  not not_2 (not_2_out[7], and_3_out);
  or or_2 (or_2_out, and_3_out, and_4_out[7]);
  and and_3 (and_3_out, ~F0, F1, ~F2);  // AND_Gate
  and and_4 (and_4_out[7], ~F0, ~F1, F2);  // AND_Gate
  Mux_8__8bit mux_8_8bit_1 (
    .in_4(A), .in_5(B), .in_6(adder_8bits_1_out_4), .in_7(adder_8bits_1_out_4), .in_8(adder_8bits_1_out_4),
    .in_9(not_1_out), .in_10(and_2_out), .in_11(or_1_out), .in_1(F2), .in_2(F1), .in_3(F0), .out_12(OUT));
  nor nor_1 (Zero, OUT[0], OUT[1], OUT[2], OUT[3], OUT[4], OUT[5], OUT[6], OUT[7]);
endmodule

// Mux 8
module Mux_8__8bit (
  input  in_1,
  input  in_2,
  input  in_3,
  input  [7:0] in_4,
  input  [7:0] in_5,
  input  [7:0] in_6,
  input  [7:0] in_7,
  input  [7:0] in_8,
  input  [7:0] in_9,
  input  [7:0] in_10,
  input  [7:0] in_11,
  output [7:0] out_12
);

  wire not_1_out, not_2_out, not_3_out;
  wire [7:0] and_9_out, and_10_out, and_11_out, and_12_out, and_13_out, and_14_out, and_15_out, and_16_out;
  wire [7:7] and_1_out, and_2_out, and_3_out, and_4_out, and_5_out, and_6_out, and_7_out, and_8_out;

  not not_1 (not_1_out, in_1);
  not not_2 (not_2_out, in_2);
  not not_3 (not_3_out, in_3);
  and and_1 (and_1_out[7], not_1_out, not_2_out, not_3_out);
  and and_2 (and_2_out[7], not_1_out, not_2_out, in_3);
  and and_3 (and_3_out[7], not_1_out, in_2, not_3_out);
  and and_4 (and_4_out[7], not_1_out, in_2, in_3);
  and and_5 (and_5_out[7], in_1, not_2_out, not_3_out);
  and and_6 (and_6_out[7], in_3, not_2_out, in_1);
  and and_7 (and_7_out[7], not_3_out, in_2, in_1);
  and and_8 (and_8_out[7], in_1, in_2, in_3);
  assign and_9_out = {8{and_1_out[7]}} & in_4;  // AND_Gate and_9, 8 bits wide
  assign and_10_out = {8{and_8_out[7]}} & in_11;  // AND_Gate and_10, 8 bits wide
  assign and_11_out = {8{and_2_out[7]}} & in_5;  // AND_Gate and_11, 8 bits wide
  assign and_12_out = {8{and_3_out[7]}} & in_6;  // AND_Gate and_12, 8 bits wide
  assign and_13_out = {8{and_6_out[7]}} & in_9;  // AND_Gate and_13, 8 bits wide
  assign and_14_out = {8{and_7_out[7]}} & in_10;  // AND_Gate and_14, 8 bits wide
  assign and_15_out = {8{and_4_out[7]}} & in_7;  // AND_Gate and_15, 8 bits wide
  assign and_16_out = {8{and_5_out[7]}} & in_8;  // AND_Gate and_16, 8 bits wide
  assign out_12 = and_9_out | and_11_out | and_12_out | and_15_out | and_16_out | and_13_out | and_14_out | and_10_out;  // OR_Gate or_1, 8 bits wide
endmodule

// Register
module Register_8bits (
  input  clk,
  input  in_enable,
  input  [7:0] \input ,
  output [7:0] \output 
);

  D_Flip_Flop d_ff_1 (.clk(clk), .D(\input [0]), .Q(\output [0]), .en(in_enable));  // open: Qn, preset, reset
  D_Flip_Flop d_ff_2 (.clk(clk), .D(\input [1]), .Q(\output [1]), .en(in_enable));  // open: Qn, preset, reset
  D_Flip_Flop d_ff_3 (.clk(clk), .D(\input [2]), .Q(\output [2]), .en(in_enable));  // open: Qn, preset, reset
  D_Flip_Flop d_ff_4 (.clk(clk), .D(\input [3]), .Q(\output [3]), .en(in_enable));  // open: Qn, preset, reset
  D_Flip_Flop d_ff_5 (.clk(clk), .D(\input [4]), .Q(\output [4]), .en(in_enable));  // open: Qn, preset, reset
  D_Flip_Flop d_ff_6 (.clk(clk), .D(\input [5]), .Q(\output [5]), .en(in_enable));  // open: Qn, preset, reset
  D_Flip_Flop d_ff_7 (.clk(clk), .D(\input [6]), .Q(\output [6]), .en(in_enable));  // open: Qn, preset, reset
  D_Flip_Flop d_ff_8 (.clk(clk), .D(\input [7]), .Q(\output [7]), .en(in_enable));  // open: Qn, preset, reset
endmodule

// CPU Mic-2
module CPU (
  input  Clk,
  input  [7:0] Input_Port,
  input  [7:0] Memory_Data__Bus_In,
  output Halt,
  output [7:0] Memory_Address_Bus,
  output [7:0] Memory_Data__Bus_Out,
  output [7:0] Output_Port,
  output RDO,
  output RDI,
  output R_I,
  output OUTI,
  output IND
);

  wire and_1_out, and_2_out, BEQ, BLT, DBO, or_1_out, PCI, RAI, RBI, sign_flag_q, zero, zero_flag_q;
  wire [1:0] MuxB;
  wire [2:0] ALU;
  wire [7:0] mux_4_8bits_1_out_7, register_8bits_1_output, register_8bits_2_output, register_8bits_3_output;

  D_Flip_Flop zero_flag (.clk(Clk), .D(zero), .Q(zero_flag_q));  // open: Qn, preset, en, reset
  D_Flip_Flop sign_flag (.clk(Clk), .D(Output_Port[7]), .Q(sign_flag_q));  // open: Qn, preset, en, reset
  and and_1 (and_1_out, zero_flag_q, BEQ);
  and and_2 (and_2_out, sign_flag_q, BLT);
  or or_1 (or_1_out, and_2_out, and_1_out, PCI);
  Register_8bits register_8bits_1 (
    .\input (Output_Port), .\output (register_8bits_1_output), .clk(Clk), .in_enable(or_1_out));
  Register_8bits register_8bits_2 (
    .\input (Output_Port), .\output (register_8bits_2_output), .clk(Clk), .in_enable(RBI));
  Register_8bits register_8bits_3 (
    .\input (Output_Port), .\output (register_8bits_3_output), .clk(Clk), .in_enable(RAI));
  LED led_1 (.in(register_8bits_1_output[7]));
  LED led_2 (.in(register_8bits_2_output[7]));
  LED led_3 (.in(register_8bits_3_output[7]));
  Pull_Resistor pull_resistor_1 (.node(Memory_Data__Bus_In[6]));
  Pull_Resistor pull_resistor_2 (.node(Memory_Data__Bus_In[7]));
  LED led_4 (.in(register_8bits_1_output[3]));
  LED led_5 (.in(register_8bits_1_output[5]));
  LED led_6 (.in(register_8bits_1_output[6]));
  LED led_7 (.in(register_8bits_1_output[4]));
  LED led_8 (.in(register_8bits_2_output[5]));
  LED led_9 (.in(register_8bits_2_output[6]));
  LED led_10 (.in(register_8bits_2_output[4]));
  LED led_11 (.in(register_8bits_2_output[3]));
  LED led_12 (.in(register_8bits_3_output[6]));
  LED led_13 (.in(register_8bits_3_output[4]));
  LED led_14 (.in(register_8bits_3_output[5]));
  LED led_15 (.in(register_8bits_3_output[3]));
  LED led_16 (.in(register_8bits_1_output[2]));
  LED led_17 (.in(register_8bits_1_output[0]));
  LED led_18 (.in(register_8bits_1_output[1]));
  LED led_19 (.in(register_8bits_2_output[0]));
  LED led_20 (.in(register_8bits_2_output[2]));
  LED led_21 (.in(register_8bits_2_output[1]));
  LED led_22 (.in(register_8bits_3_output[0]));
  LED led_23 (.in(register_8bits_3_output[2]));
  LED led_24 (.in(register_8bits_3_output[1]));
  UCC ucc_1 (
    .CLK(Clk), .OpCode(Memory_Data__Bus_In[5:0]), .MuxB(MuxB), .ALU(ALU), .IND(IND), .OUTI(OUTI), .HLT(Halt),
    .R_I(R_I), .RDI(RDI), .RDO(RDO), .DBO(DBO), .PCI(PCI), .RBI(RBI), .RAI(RAI), .BLT(BLT), .BEQ(BEQ));
  LED F2 (.in(ALU[2]));
  LED F1 (.in(ALU[1]));
  LED F0 (.in(ALU[0]));
  LED MB1 (.in(MuxB[1]));
  LED MB0 (.in(MuxB[0]));
  LED u_RAI (.in(RAI));
  LED u_RBI (.in(RBI));
  LED u_PCI (.in(PCI));
  LED u_DBO (.in(DBO));
  LED u_RDO (.in(RDO));
  LED u_RDI (.in(RDI));
  LED u_R_I (.in(R_I));
  LED HLT (.in(Halt));
  LED u_OUTI (.in(OUTI));
  LED u_IND (.in(IND));
  LED u_BEQ (.in(BEQ));
  LED u_BLT (.in(BLT));
  ALU alu_1 (
    .A(register_8bits_3_output), .B(mux_4_8bits_1_out_7), .F2(ALU[2]), .F1(ALU[1]), .F0(ALU[0]),
    .OUT(Output_Port), .Zero(zero));  // open: Cout
  LED led_25 (.in(Output_Port[7]));
  LED led_26 (.in(Output_Port[6]));
  Mux_4__8bits mux_4_8bits_1 (
    .in_3(Memory_Data__Bus_In), .in_4(Input_Port), .in_5(register_8bits_1_output),
    .in_6(register_8bits_2_output), .out_7(mux_4_8bits_1_out_7), .in_1(MuxB[1]), .in_2(MuxB[0]));
  LED led_27 (.in(Output_Port[4]));
  LED led_28 (.in(Output_Port[2]));
  LED led_29 (.in(Output_Port[5]));
  LED led_30 (.in(Output_Port[3]));
  LED led_31 (.in(mux_4_8bits_1_out_7[6]));
  LED led_32 (.in(mux_4_8bits_1_out_7[7]));
  LED led_33 (.in(Output_Port[0]));
  LED led_34 (.in(Output_Port[1]));
  LED led_35 (.in(mux_4_8bits_1_out_7[3]));
  LED led_36 (.in(mux_4_8bits_1_out_7[5]));
  LED led_37 (.in(mux_4_8bits_1_out_7[4]));
  LED led_38 (.in(mux_4_8bits_1_out_7[2]));
  LED led_39 (.in(mux_4_8bits_1_out_7[0]));
  LED led_40 (.in(mux_4_8bits_1_out_7[1]));
  Demux_2__8bits demux_2_8bits_1 (
    .in_2(Output_Port), .out_3(Memory_Data__Bus_Out), .out_4(Memory_Address_Bus), .in_1(DBO));

  // Other names for the same wires on the sheet: HLT = Halt; sign = Output_Port[7]

  // Notes on the sheet:
  //   PC
  //   B
  //   A
  //   Op Code
  //   A Bus
  //   zero
  //   Out Bus
  //   sign
  //   B Bus
  //   F2
  //   F1
  //   F0
endmodule

// Mux 4
module Mux_4__8bits (
  input  in_1,
  input  in_2,
  input  [7:0] in_3,
  input  [7:0] in_4,
  input  [7:0] in_5,
  input  [7:0] in_6,
  output [7:0] out_7
);

  wire not_1_out, not_2_out;
  wire [7:0] and_5_out, and_6_out, and_7_out, and_8_out;
  wire [7:7] and_1_out, and_2_out, and_3_out, and_4_out;

  not not_1 (not_1_out, in_1);
  not not_2 (not_2_out, in_2);
  and and_1 (and_1_out[7], in_1, in_2);
  and and_2 (and_2_out[7], in_1, not_2_out);
  and and_3 (and_3_out[7], not_1_out, in_2);
  and and_4 (and_4_out[7], not_2_out, not_1_out);
  assign and_5_out = {8{and_1_out[7]}} & in_3;  // AND_Gate and_5, 8 bits wide
  assign and_6_out = {8{and_4_out[7]}} & in_6;  // AND_Gate and_6, 8 bits wide
  assign and_7_out = {8{and_2_out[7]}} & in_4;  // AND_Gate and_7, 8 bits wide
  assign and_8_out = {8{and_3_out[7]}} & in_5;  // AND_Gate and_8, 8 bits wide
  assign out_7 = and_5_out | and_7_out | and_8_out | and_6_out;  // OR_Gate or_1, 8 bits wide
endmodule

module UCC (
  input  CLK,
  input  [5:0] OpCode,
  output BLT,
  output [1:0] MuxB,
  output IND,
  output HLT,
  output BEQ,
  output [2:0] ALU,
  output OUTI,
  output R_I,
  output RDI,
  output RDO,
  output DBO,
  output PCI,
  output RBI,
  output RAI
);

  wire not_1_out;
  wire [5:0] mux_2_6bits_1_out_4, register_8bits_2_output;
  wire [7:0] register_8bits_1_output, rom_1_data;
  wire [7:7] pull_resistor_1_node, register_8bits_3_output;
  wire [15:0] rom_1_data_2;

  Mux_2__6bits mux_2_6bits_1 (
    .in_2(register_8bits_2_output), .in_3(OpCode), .out_4(mux_2_6bits_1_out_4),
    .in_1(register_8bits_3_output[7]));
  LED led_1 (.in(OpCode[3]));
  LED led_2 (.in(OpCode[5]));
  LED led_3 (.in(OpCode[4]));
  Pull_Resistor pull_resistor_1 (.node(pull_resistor_1_node[7]));
  LED led_4 (.in(OpCode[0]));
  LED led_5 (.in(OpCode[2]));
  LED led_6 (.in(OpCode[1]));
  not not_1 (not_1_out, CLK);
  Register_8bits register_8bits_1 (
    .\input ({{2{pull_resistor_1_node[7]}}, mux_2_6bits_1_out_4}), .\output (register_8bits_1_output),
    .clk(CLK), .in_enable(1'b1));
  LED led_7 (.in(register_8bits_1_output[4]));
  LED led_8 (.in(register_8bits_1_output[5]));
  LED led_9 (.in(BLT));
  LED led_10 (.in(BEQ));
  LED led_11 (.in(register_8bits_2_output[5]));
  LED led_12 (.in(register_8bits_1_output[3]));
  LED led_13 (.in(register_8bits_1_output[2]));
  LED led_14 (.in(register_8bits_1_output[0]));
  LED led_15 (.in(register_8bits_1_output[1]));
  ROM #(.addrWidth(6), .dataWidth(24)) rom_1 (
    .addr(register_8bits_1_output[5:0]), .data({rom_1_data, rom_1_data_2}));  // open: sel
  Register_8bits register_8bits_2 (
    .\input (rom_1_data), .\output ({BLT, BEQ, register_8bits_2_output}), .clk(not_1_out), .in_enable(1'b1));
  LED led_16 (.in(register_8bits_2_output[3]));
  LED led_17 (.in(register_8bits_2_output[2]));
  LED led_18 (.in(register_8bits_2_output[1]));
  LED led_19 (.in(register_8bits_2_output[4]));
  LED led_20 (.in(register_8bits_2_output[0]));
  LED led_21 (.in(MuxB[1]));
  LED led_22 (.in(register_8bits_3_output[7]));
  Register_8bits register_8bits_3 (
    .\input (rom_1_data_2[15:8]), .\output ({register_8bits_3_output[7], MuxB, ALU, IND, OUTI}),
    .clk(not_1_out), .in_enable(1'b1));
  LED led_23 (.in(MuxB[0]));
  LED led_24 (.in(ALU[1]));
  LED led_25 (.in(ALU[0]));
  LED led_26 (.in(ALU[2]));
  LED led_27 (.in(HLT));
  LED led_28 (.in(IND));
  LED led_29 (.in(OUTI));
  Register_8bits register_8bits_4 (
    .\input (rom_1_data_2[7:0]), .\output ({HLT, R_I, RDI, RDO, DBO, PCI, RBI, RAI}), .clk(not_1_out),
    .in_enable(1'b1));
  LED led_30 (.in(DBO));
  LED led_31 (.in(RDI));
  LED led_32 (.in(RDO));
  LED led_33 (.in(R_I));
  LED led_34 (.in(RAI));
  LED led_35 (.in(PCI));
  LED led_36 (.in(RBI));

  // Notes on the sheet:
  //   Next Address
  //   MPC
  //   MP ROM
  //   contents of rom_1 (hex, n*v repeats v):
  //   12440 22804 8010 0 80 60200 4401 100 92440 a2804 b6450 6411 d2440 e2804 6411 102440 112804 126450 28
  //   4 401 2 c01 1001 1801 1c01 1401 1c2440 1d2804 1e1000 406410 202440 212804 221000 806410
  //   JMPC
  //   MIR Registers
endmodule

// Mux 2
module Mux_2__6bits (
  input  in_1,
  input  [5:0] in_2,
  input  [5:0] in_3,
  output [5:0] out_4
);

  wire [5:0] and_1_out, and_2_out;
  wire [5:5] not_1_out;

  not not_1 (not_1_out[5], in_1);
  assign and_1_out = {6{not_1_out[5]}} & in_2;  // AND_Gate and_1, 6 bits wide
  assign and_2_out = {6{in_1}} & in_3;  // AND_Gate and_2, 6 bits wide
  assign out_4 = and_1_out | and_2_out;  // OR_Gate or_1, 6 bits wide
endmodule

// Memory
module Main_Memory (
  input  Clk,
  input  R_I,
  input  RDI,
  input  RDO,
  input  [7:0] Memory_Address_Bus,
  input  [7:0] Memory_Data_Bus,
  input  run_programming_mode_switch,
  input  RAM_progamming_push_button,
  input  [7:0] progrmmable_data_inputs_switches,
  input  [7:0] programmable_address_switches,
  output [7:0] Memory_Data_Bus_2
);

  wire and_1_out, mux_2_1bits_1_out_4, not_1_out;
  wire [7:0] mux_2_8bits_1_out_4, mux_2_8bits_2_out_4, ram_256_bytes_1_uncontrolled_output_value,
       register_8bits_1_output;

  LED led_1 (.in(register_8bits_1_output[6]));
  LED led_2 (.in(register_8bits_1_output[7]));
  Register_8bits register_8bits_1 (
    .\input (Memory_Address_Bus), .\output (register_8bits_1_output), .clk(Clk), .in_enable(R_I));
  LED led_3 (.in(register_8bits_1_output[2]));
  LED led_4 (.in(register_8bits_1_output[4]));
  LED led_5 (.in(register_8bits_1_output[5]));
  LED led_6 (.in(register_8bits_1_output[3]));
  LED led_7 (.in(register_8bits_1_output[1]));
  LED led_8 (.in(register_8bits_1_output[0]));
  Mux_2__8bits mux_2_8bits_1 (
    .in_2(register_8bits_1_output), .in_3(programmable_address_switches), .out_4(mux_2_8bits_1_out_4),
    .in_1(run_programming_mode_switch));
  Mux_2__8bits mux_2_8bits_2 (
    .in_2(Memory_Data_Bus), .in_3(progrmmable_data_inputs_switches), .out_4(mux_2_8bits_2_out_4),
    .in_1(run_programming_mode_switch));
  LED run_mode_on (.in(not_1_out));
  LED programming_mode_on (.in(run_programming_mode_switch));
  not not_1 (not_1_out, run_programming_mode_switch);
  and and_1 (and_1_out, RDI, Clk);
  Mux_2__1bits mux_2_1bits_1 (
    .in_2(and_1_out), .in_3(RAM_progamming_push_button), .out_4(mux_2_1bits_1_out_4),
    .in_1(run_programming_mode_switch));
  LED led_9 (.in(ram_256_bytes_1_uncontrolled_output_value[7]));
  LED led_10 (.in(ram_256_bytes_1_uncontrolled_output_value[6]));
  RAM__256_Bytes ram_256_bytes_1 (
    .addresse(mux_2_8bits_1_out_4), .input_value(mux_2_8bits_2_out_4),
    .controlled_output_value(Memory_Data_Bus_2),
    .uncontrolled_output_value(ram_256_bytes_1_uncontrolled_output_value), .in(mux_2_1bits_1_out_4), .out(RDO));
  LED led_11 (.in(ram_256_bytes_1_uncontrolled_output_value[5]));
  LED led_12 (.in(ram_256_bytes_1_uncontrolled_output_value[2]));
  LED led_13 (.in(ram_256_bytes_1_uncontrolled_output_value[4]));
  LED led_14 (.in(ram_256_bytes_1_uncontrolled_output_value[3]));
  LED led_15 (.in(ram_256_bytes_1_uncontrolled_output_value[0]));
  LED led_16 (.in(ram_256_bytes_1_uncontrolled_output_value[1]));

  // Notes on the sheet:
  //   Memory_Data_Bus: pull=down
  //   MAR
endmodule

// Mux 2
module Mux_2__8bits (
  input  in_1,
  input  [7:0] in_2,
  input  [7:0] in_3,
  output [7:0] out_4
);

  wire [7:0] and_1_out, and_2_out;
  wire [7:7] not_1_out;

  not not_1 (not_1_out[7], in_1);
  assign and_1_out = {8{not_1_out[7]}} & in_2;  // AND_Gate and_1, 8 bits wide
  assign and_2_out = {8{in_1}} & in_3;  // AND_Gate and_2, 8 bits wide
  assign out_4 = and_1_out | and_2_out;  // OR_Gate or_1, 8 bits wide
endmodule

// Mux 2
module Mux_2__1bits (
  input  in_1,
  input  in_2,
  input  in_3,
  output out_4
);

  wire and_1_out, and_2_out, not_1_out;

  not not_1 (not_1_out, in_1);
  and and_1 (and_1_out, not_1_out, in_2);
  and and_2 (and_2_out, in_1, in_3);
  or or_1 (out_4, and_1_out, and_2_out);
endmodule

// RAM
module RAM__256_Bytes (
  input  in,
  input  out,
  input  [7:0] addresse,
  input  [7:0] input_value,
  output [7:0] controlled_output_value,
  output [7:0] uncontrolled_output_value
);

  wire and_1_out, and_2_out, nand_1_out, not_1_out, xor_1_out;

  xor xor_1 (xor_1_out, in, out);
  and and_1 (and_1_out, in, xor_1_out);
  and and_2 (and_2_out, xor_1_out, out);
  nand nand_1 (nand_1_out, and_1_out, ~and_2_out);  // NAND_Gate
  not not_1 (not_1_out, nand_1_out);
  assign uncontrolled_output_value = not_1_out ? input_value : 8'bz;  // Controlled_Buffer controlled_buffer_1
  RAM #(.bus("asynch")) ram_1 (
    .addr(addresse), .data(uncontrolled_output_value), .sel(1'b1), .ld(nand_1_out), .clr(1'b0));
  assign controlled_output_value = out ? uncontrolled_output_value : 8'bz;  // Controlled_Buffer controlled_buffer_2

  // Notes on the sheet:
  //   RAM
endmodule

// Output\n Display
module Display (
  input  CLK,
  input  OUTI,
  input  [7:0] Output_Display_Value,
  output [7:0] Ones_Digit,
  output [7:0] Tens_Digit,
  output [7:0] Hundreds_Digit,
  output [7:0] Signe_Digit
);

  wire [6:0] register_8bits_1_output;

  Register_8bits register_8bits_1 (
    .\input (Output_Display_Value), .\output ({Signe_Digit[6], register_8bits_1_output}), .clk(CLK),
    .in_enable(OUTI));
  LED led_1 (.in(Signe_Digit[6]));
  LED led_2 (.in(register_8bits_1_output[5]));
  LED led_3 (.in(register_8bits_1_output[4]));
  LED led_4 (.in(register_8bits_1_output[6]));
  LED led_5 (.in(register_8bits_1_output[3]));
  LED led_6 (.in(register_8bits_1_output[0]));
  LED led_7 (.in(register_8bits_1_output[1]));
  LED led_8 (.in(register_8bits_1_output[2]));
  ROM rom_1 (.addr({Signe_Digit[6], register_8bits_1_output}), .data(Ones_Digit));  // open: sel
  ROM rom_2 (.addr({Signe_Digit[6], register_8bits_1_output}), .data(Tens_Digit));  // open: sel
  ROM rom_3 (.addr({Signe_Digit[6], register_8bits_1_output}), .data(Hundreds_Digit));  // open: sel

  assign {Signe_Digit[7], Signe_Digit[5:0]} = {7{1'b0}};

  // Notes on the sheet:
  //   Output (OR)
  //   Ones ROM
  //   Tens ROM
  //   Hundreds ROM
  //   contents of rom_1 (hex, n*v repeats v):
  //   3f 6 5b 4f 66 6d 7d 7 7f 6f 3f 6 5b 4f 66 6d 7d 7 7f 6f 3f 6 5b 4f 66 6d 7d 7 7f 6f 3f 6 5b 4f 66 6d
  //   7d 7 7f 6f 3f 6 5b 4f 66 6d 7d 7 7f 6f 3f 6 5b 4f 66 6d 7d 7 7f 6f 3f 6 5b 4f 66 6d 7d 7 7f 6f 3f 6
  //   5b 4f 66 6d 7d 7 7f 6f 3f 6 5b 4f 66 6d 7d 7 7f 6f 3f 6 5b 4f 66 6d 7d 7 7f 6f 3f 6 5b 4f 66 6d 7d 7
  //   7f 6f 3f 6 5b 4f 66 6d 7d 7 7f 6f 3f 6 5b 4f 66 6d 7d 7 7f 7 7d 6d 66 4f 5b 6 3f 6f 7f 7 7d 6d 66 4f
  //   5b 6 3f 6f 7f 7 7d 6d 66 4f 5b 6 3f 6f 7f 7 7d 6d 66 4f 5b 6 3f 6f 7f 7 7d 6d 66 4f 5b 6 3f 6f 7f 7
  //   7d 6d 66 4f 5b 6 3f 6f 7f 7 7d 6d 66 4f 5b 6 3f 6f 7f 7 7d 6d 66 4f 5b 6 3f 6f 7f 7 7d 6d 66 4f 5b 6
  //   3f 6f 7f 7 7d 6d 66 4f 5b 6 3f 6f 7f 7 7d 6d 66 4f 5b 6 3f 6f 7f 7 7d 6d 66 4f 5b 6 3f 6f 7f 7 7d 6d
  //   66 4f 5b 6
  //   contents of rom_2 (hex, n*v repeats v):
  //   10*3f 10*6 10*5b 10*4f 10*66 10*6d 10*7d 10*7 10*7f 10*6f 10*3f 10*6 17*5b 10*6 10*3f 10*6f 10*7f
  //   10*7 10*7d 10*6d 10*66 10*4f 10*5b 10*6 9*3f
  //   contents of rom_3 (hex, n*v repeats v):
  //   100*3f 57*6 99*3f
endmodule

// Binary\n keyboard
module Keyboard_Input (
  input  IND,
  input  [7:0] Binary_Keyboard,
  input  Enter_Push_Button,
  output HLT,
  output Read_State_Indicator,
  output [7:0] Keyboard_Value
);

  wire d_ff_1_qn, not_1_out;

  LED led_1 (.in(Keyboard_Value[5]));
  LED led_2 (.in(Keyboard_Value[6]));
  LED led_3 (.in(Keyboard_Value[7]));
  and and_1 (HLT, IND, d_ff_1_qn);
  not not_1 (not_1_out, IND);
  Register_8bits register_8bits_1 (
    .\input (Binary_Keyboard), .\output (Keyboard_Value), .clk(Enter_Push_Button), .in_enable(1'b1));
  LED led_4 (.in(Keyboard_Value[1]));
  LED led_5 (.in(Keyboard_Value[3]));
  LED led_6 (.in(Keyboard_Value[4]));
  LED led_7 (.in(Keyboard_Value[2]));
  LED led_8 (.in(Keyboard_Value[0]));
  D_Flip_Flop d_ff_1 (
    .clk(not_1_out), .D(1'b0), .Q(Read_State_Indicator), .Qn(d_ff_1_qn), .preset(Enter_Push_Button));  // open: en, reset

  // Notes on the sheet:
  //   Input (IR)
  //   Read State Memory
endmodule

module Clock (
  input  clk,
  input  switch,
  input  manual,
  input  hlt,
  output clock_output
);

  wire and_1_out, and_2_out, not_1_out, not_2_out, or_1_out;

  not not_1 (not_1_out, switch);
  not not_2 (not_2_out, hlt);
  and and_1 (and_1_out, clk, switch);
  and and_2 (and_2_out, not_1_out, manual);
  or or_1 (or_1_out, and_1_out, and_2_out);
  and and_3 (clock_output, or_1_out, not_2_out);

  // Notes on the sheet:
  //   manual: pull=down
  //   hlt: pull=down
endmodule

module Branchement (
  input  [2:0] in_1,
  input  [1:0] in_2,
  output out_3
);

  wire and_1_out, and_2_out;

  and and_1 (and_1_out, in_1[2], ~in_1[1], ~in_1[0]);  // AND_Gate
  and and_2 (and_2_out, ~in_2[0], ~in_2[1]);  // AND_Gate
  and and_3 (out_3, and_1_out, and_2_out);
endmodule

// Demux
module Demux_2__8bits (
  input  in_1,
  input  [7:0] in_2,
  output [7:0] out_3,
  output [7:0] out_4
);

  wire not_1_out;

  not not_1 (not_1_out, in_1);
  assign out_3 = in_1 ? in_2 : 8'bz;  // Controlled_Buffer controlled_buffer_1
  assign out_4 = not_1_out ? in_2 : 8'bz;  // Controlled_Buffer controlled_buffer_2
endmodule
